// Digital circuit ALU_32.dig as structural Verilog
module ALU_32 (
  input  [31:0] A_32,
  input  [31:0] B_32,
  input  [3:0] OPCODE,
  output [31:0] R_32
);

  wire [31:0] multiplexer_1_out, multiplexer_2_out, nand_1_out, not_1_out, not_2_out, not_3_out;

  assign not_1_out = ~A_32;  // Not not_1, 32 bits wide
  assign not_2_out = ~B_32;  // Not not_2, 32 bits wide
  Multiplexer #(.Bits(32)) multiplexer_1 (.sel(OPCODE[0]), .in_0(A_32), .in_1(not_1_out), .out(multiplexer_1_out));
  Multiplexer #(.Bits(32)) multiplexer_2 (.sel(OPCODE[0]), .in_0(B_32), .in_1(not_2_out), .out(multiplexer_2_out));
  assign nand_1_out = ~(multiplexer_1_out & multiplexer_2_out);  // NAnd nand_1, 32 bits wide
  assign not_3_out = ~nand_1_out;  // Not not_3, 32 bits wide
  Multiplexer #(.Bits(32)) multiplexer_3 (.sel(OPCODE[1]), .in_0(nand_1_out), .in_1(not_3_out), .out(R_32));

  // Notes on the sheet:
  //   0000	NAND
  //   0001	OR
  //   0010	AND
  //   0011	NOR
endmodule

/* Test case LOGIC:
OPCODE A_32 B_32 R_32
loop(i,10000)
 let a = random(1<<32);
 let b = random(1<<32);
(0)	(a)	(b)	(~(a&b))
(1)	(a)	(b)	(a|b)
(2)	(a)	(b)	(a&b)
(3)	(a)	(b)	(~(a|b))

end loop
*/
