// Digital circuit CLA.dig as structural Verilog
module CLA (
  input  P_0,
  input  P_1,
  input  P_2,
  input  P_3,
  input  G_0,
  input  G_1,
  input  G_2,
  input  G_3,
  input  C_0,
  output GG,
  output C_1,
  output C_2,
  output C_3,
  output PG
);

  wire and_1_out, and_2_out, and_3_out, and_4_out, and_5_out, and_6_out, and_7_out, and_8_out, and_9_out,
       and_10_out, and_11_out, or_2_out, or_4_out, or_5_out, or_6_out, or_7_out;

  and and_1 (and_1_out, G_2, P_3);
  and and_2 (and_2_out, C_0, P_0);
  and and_3 (and_3_out, G_0, P_1);
  and and_4 (and_4_out, G_1, P_2);
  or or_1 (C_1, and_2_out, G_0);
  and and_5 (and_5_out, and_2_out, P_1);
  and and_6 (and_6_out, and_3_out, P_2);
  and and_7 (and_7_out, and_4_out, P_3);
  or or_2 (or_2_out, and_3_out, and_5_out);
  and and_8 (and_8_out, and_5_out, P_2);
  and and_9 (and_9_out, and_6_out, P_3);
  or or_3 (C_2, or_2_out, G_1);
  or or_4 (or_4_out, and_4_out, and_6_out);
  or or_5 (or_5_out, and_1_out, and_7_out);
  or or_6 (or_6_out, or_4_out, and_8_out);
  or or_7 (or_7_out, or_5_out, and_9_out);
  or or_8 (C_3, or_6_out, G_2);
  or or_9 (GG, or_7_out, G_3);
  and and_10 (and_10_out, P_0, P_1);
  and and_11 (and_11_out, P_2, P_3);
  and and_12 (PG, and_10_out, and_11_out);
endmodule
