// Digital circuit CLA8.dig as structural Verilog
module CLA8 (
  input  P_0,
  input  G_0,
  input  C_0,
  input  P_1,
  input  G_1,
  input  P_2,
  input  G_2,
  input  P_3,
  input  G_3,
  input  P_4,
  input  G_4,
  input  P_5,
  input  G_5,
  input  P_6,
  input  G_6,
  input  P_7,
  input  G_7,
  output PG,
  output GG,
  output C_1,
  output C_2,
  output C_3,
  output C_4,
  output C_5,
  output C_6,
  output C_7
);

  wire and_1_out, and_2_out, and_3_out, and_4_out, and_5_out, and_6_out, and_7_out, and_8_out, and_9_out,
       and_10_out, and_11_out, and_12_out, and_13_out, and_14_out, and_15_out, and_16_out, and_17_out,
       and_18_out, and_19_out, and_20_out, and_21_out, and_22_out, and_23_out, and_24_out, and_25_out,
       and_26_out, and_27_out, and_28_out, and_30_out, and_31_out, and_32_out, and_33_out, and_34_out,
       and_35_out, and_36_out, and_37_out, and_38_out, and_39_out, and_40_out, and_41_out, and_42_out,
       or_2_out, or_4_out, or_5_out, or_7_out, or_8_out, or_9_out, or_10_out, or_11_out, or_13_out,
       or_14_out, or_15_out, or_17_out, or_18_out, or_19_out, or_20_out, or_21_out, or_22_out, or_23_out,
       or_24_out, or_25_out, or_26_out, or_27_out, or_28_out, or_30_out, or_31_out, or_32_out, or_33_out;

  and and_1 (and_1_out, P_0, P_1);
  and and_2 (and_2_out, and_1_out, P_2);
  and and_3 (and_3_out, and_2_out, P_3);
  and and_4 (and_4_out, G_3, P_4);
  and and_5 (and_5_out, G_4, P_5);
  and and_6 (and_6_out, G_5, P_6);
  and and_7 (and_7_out, G_6, P_7);
  and and_8 (and_8_out, and_3_out, P_4);
  and and_9 (and_9_out, C_0, P_0);
  and and_10 (and_10_out, G_0, P_1);
  and and_11 (and_11_out, G_1, P_2);
  and and_12 (and_12_out, G_2, P_3);
  and and_13 (and_13_out, and_4_out, P_5);
  and and_14 (and_14_out, and_5_out, P_6);
  and and_15 (and_15_out, and_6_out, P_7);
  and and_16 (and_16_out, and_8_out, P_5);
  and and_17 (and_17_out, and_9_out, P_1);
  and and_18 (and_18_out, and_10_out, P_2);
  and and_19 (and_19_out, and_11_out, P_3);
  and and_20 (and_20_out, and_12_out, P_4);
  and and_21 (and_21_out, and_13_out, P_6);
  and and_22 (and_22_out, and_14_out, P_7);
  and and_23 (and_23_out, and_16_out, P_6);
  or or_1 (C_1, and_9_out, G_0);
  and and_24 (and_24_out, and_17_out, P_2);
  and and_25 (and_25_out, and_18_out, P_3);
  and and_26 (and_26_out, and_19_out, P_4);
  and and_27 (and_27_out, and_20_out, P_5);
  and and_28 (and_28_out, and_21_out, P_7);
  and and_29 (PG, and_23_out, P_7);
  or or_2 (or_2_out, and_10_out, and_17_out);
  or or_3 (C_2, or_2_out, G_1);
  or or_4 (or_4_out, and_11_out, and_18_out);
  and and_30 (and_30_out, and_24_out, P_3);
  and and_31 (and_31_out, and_25_out, P_4);
  and and_32 (and_32_out, and_26_out, P_5);
  and and_33 (and_33_out, and_27_out, P_6);
  or or_5 (or_5_out, or_4_out, and_24_out);
  or or_6 (C_3, or_5_out, G_2);
  or or_7 (or_7_out, and_12_out, and_19_out);
  or or_8 (or_8_out, or_7_out, and_25_out);
  or or_9 (or_9_out, and_4_out, and_20_out);
  and and_34 (and_34_out, and_30_out, P_4);
  and and_35 (and_35_out, and_31_out, P_5);
  and and_36 (and_36_out, and_32_out, P_6);
  and and_37 (and_37_out, and_33_out, P_7);
  or or_10 (or_10_out, or_8_out, and_30_out);
  or or_11 (or_11_out, or_9_out, and_26_out);
  and and_38 (and_38_out, and_34_out, P_5);
  and and_39 (and_39_out, and_35_out, P_6);
  and and_40 (and_40_out, and_36_out, P_7);
  or or_12 (C_4, or_10_out, G_3);
  or or_13 (or_13_out, or_11_out, and_31_out);
  or or_14 (or_14_out, and_5_out, and_13_out);
  and and_41 (and_41_out, and_38_out, P_6);
  and and_42 (and_42_out, and_39_out, P_7);
  or or_15 (or_15_out, or_13_out, and_34_out);
  or or_16 (C_5, or_15_out, G_4);
  or or_17 (or_17_out, or_14_out, and_27_out);
  or or_18 (or_18_out, or_17_out, and_32_out);
  or or_19 (or_19_out, and_6_out, and_14_out);
  or or_20 (or_20_out, and_7_out, and_15_out);
  or or_21 (or_21_out, or_18_out, and_35_out);
  or or_22 (or_22_out, or_19_out, and_21_out);
  or or_23 (or_23_out, or_20_out, and_22_out);
  or or_24 (or_24_out, or_21_out, and_38_out);
  or or_25 (or_25_out, or_22_out, and_33_out);
  or or_26 (or_26_out, or_25_out, and_36_out);
  or or_27 (or_27_out, or_23_out, and_28_out);
  or or_28 (or_28_out, or_27_out, and_37_out);
  or or_29 (C_6, or_24_out, G_5);
  or or_30 (or_30_out, or_26_out, and_39_out);
  or or_31 (or_31_out, or_28_out, and_40_out);
  or or_32 (or_32_out, or_30_out, and_41_out);
  or or_33 (or_33_out, or_31_out, and_42_out);
  or or_34 (C_7, or_32_out, G_6);
  or or_35 (GG, or_33_out, G_7);
endmodule
