// Digital circuit HA.dig as structural Verilog
module HA (
  input  A,
  input  B,
  output P,
  output G
);

  xor xor_1 (P, A, B);
  and and_1 (G, A, B);
endmodule

/* Test case:
A B G P
0 0 0 0 
1 0 0 1
0 1 0 1
1 1 1 0
*/
