// Digital circuit add16_CLA.dig as structural Verilog
module add16_CLA (
  input  [15:0] A_16,
  input  [15:0] B_16,
  input  C_in,
  output [15:0] S_16,
  output GG,
  output PG
);

  wire add4_cla_1_gg, add4_cla_1_pg, add4_cla_2_gg, add4_cla_2_pg, add4_cla_3_gg, add4_cla_3_pg,
       add4_cla_4_gg, add4_cla_4_pg, cla_1_c_1, cla_1_c_2, cla_1_c_3;

  add4_CLA add4_cla_1 (
    .C_in(C_in), .A_4(A_16[3:0]), .B_4(B_16[3:0]), .S_4(S_16[3:0]), .GG(add4_cla_1_gg), .PG(add4_cla_1_pg));
  add4_CLA add4_cla_2 (
    .C_in(cla_1_c_1), .A_4(A_16[7:4]), .B_4(B_16[7:4]), .S_4(S_16[7:4]), .GG(add4_cla_2_gg),
    .PG(add4_cla_2_pg));
  add4_CLA add4_cla_3 (
    .C_in(cla_1_c_2), .A_4(A_16[11:8]), .B_4(B_16[11:8]), .S_4(S_16[11:8]), .GG(add4_cla_3_gg),
    .PG(add4_cla_3_pg));
  add4_CLA add4_cla_4 (
    .C_in(cla_1_c_3), .A_4(A_16[15:12]), .B_4(B_16[15:12]), .S_4(S_16[15:12]), .GG(add4_cla_4_gg),
    .PG(add4_cla_4_pg));
  CLA cla_1 (
    .C_0(C_in), .P_0(add4_cla_1_pg), .G_0(add4_cla_1_gg), .P_1(add4_cla_2_pg), .G_1(add4_cla_2_gg),
    .P_2(add4_cla_3_pg), .G_2(add4_cla_3_gg), .P_3(add4_cla_4_pg), .G_3(add4_cla_4_gg), .C_1(cla_1_c_1),
    .C_2(cla_1_c_2), .C_3(cla_1_c_3), .GG(GG), .PG(PG));
endmodule
