// Digital circuit add32_CLA.dig as structural Verilog
module add32_CLA (
  input  [31:0] A_32,
  input  [31:0] B_32,
  input  C_in,
  output C_out,
  output [31:0] S_32
);

  wire add4_cla_1_gg, add4_cla_1_pg, add4_cla_2_gg, add4_cla_2_pg, add4_cla_3_gg, add4_cla_3_pg,
       add4_cla_4_gg, add4_cla_4_pg, add4_cla_5_gg, add4_cla_5_pg, add4_cla_6_gg, add4_cla_6_pg,
       add4_cla_7_gg, add4_cla_7_pg, add4_cla_8_gg, add4_cla_8_pg, and_1_out, cla8_1_c_1, cla8_1_c_2,
       cla8_1_c_3, cla8_1_c_4, cla8_1_c_5, cla8_1_c_6, cla8_1_c_7, cla8_1_gg, cla8_1_pg;

  add4_CLA add4_cla_1 (
    .C_in(C_in), .A_4(A_32[3:0]), .B_4(B_32[3:0]), .S_4(S_32[3:0]), .GG(add4_cla_1_gg), .PG(add4_cla_1_pg));
  add4_CLA add4_cla_2 (
    .C_in(cla8_1_c_1), .A_4(A_32[7:4]), .B_4(B_32[7:4]), .S_4(S_32[7:4]), .GG(add4_cla_2_gg),
    .PG(add4_cla_2_pg));
  add4_CLA add4_cla_3 (
    .C_in(cla8_1_c_2), .A_4(A_32[11:8]), .B_4(B_32[11:8]), .S_4(S_32[11:8]), .GG(add4_cla_3_gg),
    .PG(add4_cla_3_pg));
  add4_CLA add4_cla_4 (
    .C_in(cla8_1_c_3), .A_4(A_32[15:12]), .B_4(B_32[15:12]), .S_4(S_32[15:12]), .GG(add4_cla_4_gg),
    .PG(add4_cla_4_pg));
  add4_CLA add4_cla_5 (
    .C_in(cla8_1_c_4), .A_4(A_32[19:16]), .B_4(B_32[19:16]), .S_4(S_32[19:16]), .GG(add4_cla_5_gg),
    .PG(add4_cla_5_pg));
  add4_CLA add4_cla_6 (
    .C_in(cla8_1_c_5), .A_4(A_32[23:20]), .B_4(B_32[23:20]), .S_4(S_32[23:20]), .GG(add4_cla_6_gg),
    .PG(add4_cla_6_pg));
  add4_CLA add4_cla_7 (
    .C_in(cla8_1_c_6), .A_4(A_32[27:24]), .B_4(B_32[27:24]), .S_4(S_32[27:24]), .GG(add4_cla_7_gg),
    .PG(add4_cla_7_pg));
  add4_CLA add4_cla_8 (
    .C_in(cla8_1_c_7), .A_4(A_32[31:28]), .B_4(B_32[31:28]), .S_4(S_32[31:28]), .GG(add4_cla_8_gg),
    .PG(add4_cla_8_pg));
  CLA8 cla8_1 (
    .C_0(C_in), .P_0(add4_cla_1_pg), .G_0(add4_cla_1_gg), .P_1(add4_cla_2_pg), .G_1(add4_cla_2_gg),
    .P_2(add4_cla_3_pg), .G_2(add4_cla_3_gg), .P_3(add4_cla_4_pg), .G_3(add4_cla_4_gg), .P_4(add4_cla_5_pg),
    .G_4(add4_cla_5_gg), .P_5(add4_cla_6_pg), .G_5(add4_cla_6_gg), .P_6(add4_cla_7_pg), .G_6(add4_cla_7_gg),
    .P_7(add4_cla_8_pg), .G_7(add4_cla_8_gg), .C_1(cla8_1_c_1), .C_2(cla8_1_c_2), .C_3(cla8_1_c_3),
    .C_4(cla8_1_c_4), .C_5(cla8_1_c_5), .C_6(cla8_1_c_6), .C_7(cla8_1_c_7), .GG(cla8_1_gg), .PG(cla8_1_pg));
  and and_1 (and_1_out, cla8_1_pg, C_in);
  or or_1 (C_out, cla8_1_gg, and_1_out);
endmodule

/* Test case:
C_in A_32 B_32 S_32 C_out
0 0 0 0 0
0 1 1 2 0
0 2 3 5 0
0 5 5 10 0
0 7 8 15 0
0 8 8 16 0
0 15 1 16 0
0 255 1 256 0
0 4095 1 4096 0
0 65534 1 65535 0
0 65535 0 65535 0
0 65535 1 65536 0
0 65535 65535 131070 0
0 21845 21845 43690 0
0 43690 21845 65535 0
0 13107 52428 65535 0
0 32767 1 32768 0
0 32768 32768 65536 0
0 61440 4095 65535 0
1 0 0 1 0
1 1 1 3 0
1 2 3 6 0
1 5 5 11 0
1 7 8 16 0
1 8 8 17 0
1 15 1 17 0
1 255 1 257 0
1 4095 1 4097 0
1 65534 1 65536 0
1 65535 0 65536 0
1 65535 1 65537 0
1 65535 65535 131071 0
1 21845 21845 43691 0
1 43690 21845 65536 0
1 13107 52428 65536 0
1 32767 1 32769 0
1 32768 32768 65537 0
1 61440 4095 65536 0
0 1253094399 3662427518 620554621 1
1 2207069130 857388540 3064457671 0
1 2942639119 2184407023 832078847 1
1 1285636725 3118482490 109151920 1
1 1381088972 589945555 1971034528 0
1 2599237505 3690455075 1994725285 1
0 464530394 1502826604 1967356998 0
1 4097088703 4168327287 3970448695 1
1 3029728230 415332651 3445060882 0
0 2345636404 803413559 3149049963 0
0 3037817083 3374465524 2117315311 1
1 229972521 2679861811 2909834333 0
1 1453925078 706817827 2160742906 0
1 2443397644 2525595437 674025786 1
1 593671146 4197804528 496508379 1
0 1955468848 1962874523 3918343371 0
1 564899852 819345145 1384244998 0
1 471590023 3948851790 125474518 1
1 666166227 3738391468 109590400 1
0 4154509304 2893423771 2752965779 1
0 3470346042 2149458306 1324837052 1
1 3488255027 2421453274 1614741006 1
0 37828949 2098928637 2136757586 0
0 2195518967 1912099823 4107618790 0
1 1223531973 3546769579 475334257 1
0 1028550646 507938669 1536489315 0
1 1978718119 4108966306 1792717130 1
0 3900007646 1944796805 1549837155 1
0 2556123461 1829050293 90206458 1
0 611023636 4054651187 370707527 1
0 1229042402 2969046088 4198088490 0
1 3413027554 213365679 3626393234 0
0 2995827553 3362688960 2063549217 1
1 3217927134 2840253424 1763213263 1
0 2133711351 374809332 2508520683 0
0 2693660631 2722079431 1120772766 1
1 3438437110 1853109051 996578866 1
0 7819257 677782577 685601834 0
1 2674845229 1608741040 4283586270 0
1 412611615 1572961819 1985573435 0
0 685589410 2847203871 3532793281 0
1 463619229 2353939849 2817559079 0
1 3963254892 1344525715 1012813312 1
0 3976678145 3665396074 3347106923 1
1 198278263 3279121881 3477400145 0
0 181086987 150237641 331324628 0
0 103200469 1082547727 1185748196 0
1 3251160771 1873896374 830089850 1
0 415387879 1605621035 2021008914 0
1 3777346391 3629880737 3112259833 1
0 2238240312 356762390 2595002702 0
0 1095536774 1623831865 2719368639 0
0 4052521276 2309554471 2067108451 1
0 1333878064 2560119825 3893997889 0
0 1947330384 3233176805 885539893 1
1 139988507 2323806029 2463794537 0
0 3865463059 1588755556 1159251319 1
0 3885138384 221768674 4106907058 0
1 3848758124 870148595 423939424 1
0 3216872522 1401720382 323625608 1
0 4289985040 362000340 357018084 1
0 104377410 2633398992 2737776402 0
0 396278697 882218060 1278496757 0
0 1131671852 3348080299 184784855 1
0 736101302 3115316850 3851418152 0
1 3245841521 257623775 3503465297 0
0 3776432250 1734797760 1216262714 1
1 2340982119 1996580302 42595126 1
0 966370899 1328098708 2294469607 0
1 1278590415 2461419736 3740010152 0
0 1504466238 4257722566 1467221508 1
1 2536743373 1380744976 3917488350 0
0 3194525156 2450089729 1349647589 1
1 3324404140 780996476 4105400617 0
0 2101901407 3207912628 1014846739 1
0 2213438478 2982983399 901454581 1
1 3492590731 1483068394 680691830 1
0 3708661272 476200235 4184861507 0
0 2017415126 278260398 2295675524 0
0 3007083793 2592648821 1304765318 1
0 298247367 120162415 418409782 0
1 603863506 2154307777 2758171284 0
1 1870588093 3095222011 670842809 1
0 3979578218 3530602844 3215213766 1
0 3171619735 4148376591 3025029030 1
0 2733178713 2192896024 631107441 1
1 2716315304 934046317 3650361622 0
1 2533039065 135996432 2669035498 0
1 734141519 2263446959 2997588479 0
0 248413575 2225209596 2473623171 0
1 636093691 2745196271 3381289963 0
1 3237398518 3145861714 2088292937 1
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*/
