// Digital circuit add4_CLA.dig as structural Verilog
module add4_CLA (
  input  [3:0] A_4,
  input  [3:0] B_4,
  input  C_in,
  output [3:0] S_4,
  output GG,
  output PG
);

  wire cla_1_c_1, cla_1_c_2, cla_1_c_3, ha_1_g, ha_1_p, ha_2_g, ha_2_p, ha_3_g, ha_3_p, ha_4_g, ha_4_p;

  HA ha_1 (.A(A_4[0]), .B(B_4[0]), .P(ha_1_p), .G(ha_1_g));
  HA ha_2 (.A(A_4[1]), .B(B_4[1]), .P(ha_2_p), .G(ha_2_g));
  HA ha_3 (.A(A_4[2]), .B(B_4[2]), .P(ha_3_p), .G(ha_3_g));
  HA ha_4 (.A(A_4[3]), .B(B_4[3]), .P(ha_4_p), .G(ha_4_g));
  CLA cla_1 (
    .C_0(C_in), .P_0(ha_1_p), .G_0(ha_1_g), .P_1(ha_2_p), .G_1(ha_2_g), .P_2(ha_3_p), .G_2(ha_3_g),
    .P_3(ha_4_p), .G_3(ha_4_g), .C_1(cla_1_c_1), .C_2(cla_1_c_2), .C_3(cla_1_c_3), .GG(GG), .PG(PG));
  xor xor_1 (S_4[0], ha_1_p, C_in);
  xor xor_2 (S_4[1], ha_2_p, cla_1_c_1);
  xor xor_3 (S_4[2], ha_3_p, cla_1_c_2);
  xor xor_4 (S_4[3], ha_4_p, cla_1_c_3);
endmodule
